// Logisim project CPU8b.circ as structural Verilog: 14 circuits, main circuit main
module main (
  input  clear
);

  wire alu_1_t, clock_1_out, control_unit_1_branch, control_unit_1_is_imm, control_unit_1_jsr,
       control_unit_1_jump, control_unit_1_pc_load, control_unit_1_ram_load, control_unit_1_ram_to_reg,
       control_unit_1_ram_wri, control_unit_1_ret, control_unit_1_unsigned__signed, control_unit_1_wrien;
  wire [2:0] control_unit_1_alu_opcode, control_unit_1_alu_shamt, control_unit_1_cond,
       control_unit_1_readaddra, control_unit_1_readaddrb, control_unit_1_wriaddr;
  wire [7:0] alu_1_result, control_unit_1_imm, multiplexer_1_out, multiplexer_2_out, pc_1_pc, ram_1_data,
       register_file_1_douta, register_file_1_doutb;
  wire [31:0] rom_1_data;

  control_unit control_unit_1 (
    .in_1(rom_1_data), .T(alu_1_t), .Jump(control_unit_1_jump), .Branch(control_unit_1_branch),
    .RET(control_unit_1_ret), .JSR(control_unit_1_jsr), .WriAddr(control_unit_1_wriaddr),
    .ReadAddrA(control_unit_1_readaddra), .ReadAddrB(control_unit_1_readaddrb), .WriEn(control_unit_1_wrien),
    .ALU_shamt(control_unit_1_alu_shamt), .ALU_opcode(control_unit_1_alu_opcode),
    .UnSigned__Signed(control_unit_1_unsigned__signed), .COND(control_unit_1_cond), .Imm(control_unit_1_imm),
    .is_imm(control_unit_1_is_imm), .RAM_Wri(control_unit_1_ram_wri), .RAM_load(control_unit_1_ram_load),
    .RAM_to_Reg(control_unit_1_ram_to_reg), .PC_load(control_unit_1_pc_load));
  Clock clock_1 (.out(clock_1_out));
  PC pc_1 (
    .offest(control_unit_1_imm), .Imm(control_unit_1_imm), .Jump(control_unit_1_jump),
    .Branch(control_unit_1_branch), .Clk(clock_1_out), .PC_load(control_unit_1_pc_load), .clear(clear),
    .PC(pc_1_pc), .JSR(control_unit_1_jsr), .RET(control_unit_1_ret));
  register_file register_file_1 (
    .Din(multiplexer_2_out), .readAddrA(control_unit_1_readaddra), .WriAddr(control_unit_1_wriaddr),
    .readAddrB(control_unit_1_readaddrb), .Clock(clock_1_out), .ClearAll(clear),
    .DoutA(register_file_1_douta), .DoutB(register_file_1_doutb), .WriEn(control_unit_1_wrien));
  ROM #(.dataWidth(32)) rom_1 (.addr(pc_1_pc), .data(rom_1_data));  // open: sel
  Multiplexer #(.width(8), .enable("false")) multiplexer_1 (
    .in0(register_file_1_doutb), .in1(control_unit_1_imm), .out(multiplexer_1_out),
    .sel(control_unit_1_is_imm));
  ALU alu_1 (
    .A(register_file_1_douta), .B(multiplexer_1_out), .shamt(control_unit_1_alu_shamt),
    .opcode(control_unit_1_alu_opcode), .result(alu_1_result), .unsign_sign(control_unit_1_unsigned__signed),
    .COND__0____1____2___3____4___5____6_ve__7_ve(control_unit_1_cond), .T(alu_1_t));
  RAM #(.bus("separate")) ram_1 (
    .addr(alu_1_result), .din(register_file_1_doutb), .data(ram_1_data), .str(control_unit_1_ram_wri),
    .clk(clock_1_out), .ld(control_unit_1_ram_load), .clr(clear));  // open: sel
  Multiplexer #(.width(8), .enable("false")) multiplexer_2 (
    .in0(alu_1_result), .in1(ram_1_data), .out(multiplexer_2_out), .sel(control_unit_1_ram_to_reg));

  // Notes on the sheet:
  //   contents of rom_1 (hex, n*v repeats v):
  //   20000343 800005 200001c3 800045 20000004 40000044 60000003 80201d6 88040041 10020096 6c800000
  //   241a0002 481c0002 1c8 2c000001 800085 20000004 40000044 60000003 a0000203 6c1a0002 84042001 10020096
  //   6c060041 241a0002 d0280d0 6d020000 24060041 b4003fc1 14027dd6 8000c5 20000004 40000044 60000003
  //   a0000203 6c1a0002 84042001 10020096 6c060041 241a0002 d0280d0 6d020000 24060041 b4003fc1 14027dd6
  //   2c000001 800105 20000c43 803f85 20000cc3 803f85 20000a83 803f85 20000dc3 803f85 20000803 803f85
  //   20000f43 803f85 20000803 803f85 20000084 444c0002 480403c1 60000283 98280d6 48000dc1 1148 48000c01
  //   1003f85 44000001 480403c1 60000283 98280d6 48000dc1 1348 48000c01 1003f85 20000283 803f85 20000c43
  //   803f85 20000cc3 803f85 20000bc3 803f85 20000dc3 803f85 20000803 803f85 20000f43 803f85 20000803
  //   803f85 200000c4 444c0002 480403c1 60000283 98280d6 48000dc1 1988 48000c01 1003f85 44000001 480403c1
  //   60000283 98280d6 48000dc1 1b88 48000c01 1003f85 20000283 803f85 20000c43 803f85 20000cc3 803f85
  //   20000943 803f85 20000dc3 803f85 20000803 803f85 20000f43 803f85 20000803 803f85 20000104 444c0002
  //   480403c1 60000283 98280d6 48000dc1 21c8 48000c01 1003f85 44000001 480403c1 60000283 98280d6 48000dc1
  //   23c8 48000c01 1003f85 20000283 803f85 20000043 803fc5 2508
endmodule

module FA (
  input  A,
  input  B,
  input  Cin,
  output sum,
  output Cout
);

  wire and_1_out, and_2_out, xor_1_out;

  xor xor_1 (xor_1_out, A, B);
  and and_1 (and_1_out, B, A);
  xor xor_2 (sum, xor_1_out, Cin);
  and and_2 (and_2_out, xor_1_out, Cin);
  or or_1 (Cout, and_2_out, and_1_out);
endmodule

module adder_8b (
  input  [7:0] A,
  input  [7:0] B,
  input  Sub,
  output Zero,
  output minus_VE,
  output Carry,
  output Overflow,
  output [7:0] out_8
);

  wire fa_2_cout, fa_3_cout, fa_4_cout, fa_5_cout, fa_6_cout, fa_7_cout, fa_8_cout, xor_1_out, xor_2_out,
       xor_3_out, xor_4_out, xor_5_out, xor_6_out, xor_7_out, xor_8_out;

  FA fa_1 (.A(A[7]), .B(xor_1_out), .Cin(fa_2_cout), .sum(minus_VE), .Cout(Carry));
  xor xor_1 (xor_1_out, B[7], Sub);
  FA fa_2 (.A(A[6]), .B(xor_2_out), .Cin(fa_3_cout), .sum(out_8[6]), .Cout(fa_2_cout));
  xor xor_2 (xor_2_out, B[6], Sub);
  FA fa_3 (.A(A[5]), .B(xor_3_out), .Cin(fa_4_cout), .sum(out_8[5]), .Cout(fa_3_cout));
  xor xor_3 (xor_3_out, B[5], Sub);
  FA fa_4 (.A(A[4]), .B(xor_4_out), .Cin(fa_5_cout), .sum(out_8[4]), .Cout(fa_4_cout));
  xor xor_4 (xor_4_out, B[4], Sub);
  FA fa_5 (.A(A[3]), .B(xor_5_out), .Cin(fa_6_cout), .sum(out_8[3]), .Cout(fa_5_cout));
  xor xor_5 (xor_5_out, B[3], Sub);
  FA fa_6 (.A(A[2]), .B(xor_6_out), .Cin(fa_7_cout), .sum(out_8[2]), .Cout(fa_6_cout));
  xor xor_6 (xor_6_out, B[2], Sub);
  FA fa_7 (.A(A[1]), .B(xor_7_out), .Cin(fa_8_cout), .sum(out_8[1]), .Cout(fa_7_cout));
  xor xor_7 (xor_7_out, B[1], Sub);
  FA fa_8 (.A(A[0]), .B(xor_8_out), .Cin(Sub), .sum(out_8[0]), .Cout(fa_8_cout));
  xor xor_8 (xor_8_out, B[0], Sub);
  xor xor_9 (Overflow, Carry, fa_2_cout);
  nor nor_1 (Zero, minus_VE, out_8[6], out_8[5], out_8[4], out_8[3], out_8[2], out_8[1], out_8[0]);

  assign out_8[7] = minus_VE;
endmodule

module XOR_8b (
  input  [7:0] in_1,
  input  [7:0] in_2,
  output [7:0] out_3
);

  xor xor_1 (out_3[7], in_2[7], in_1[7]);
  xor xor_2 (out_3[6], in_2[6], in_1[6]);
  xor xor_3 (out_3[5], in_2[5], in_1[5]);
  xor xor_4 (out_3[4], in_2[4], in_1[4]);
  xor xor_5 (out_3[3], in_2[3], in_1[3]);
  xor xor_6 (out_3[2], in_2[2], in_1[2]);
  xor xor_7 (out_3[1], in_2[1], in_1[1]);
  xor xor_8 (out_3[0], in_2[0], in_1[0]);
endmodule

module AND_8b (
  input  [7:0] in_1,
  input  [7:0] in_2,
  output [7:0] out_3
);

  and and_1 (out_3[7], in_2[7], in_1[7]);
  and and_2 (out_3[6], in_2[6], in_1[6]);
  and and_3 (out_3[5], in_2[5], in_1[5]);
  and and_4 (out_3[4], in_2[4], in_1[4]);
  and and_5 (out_3[3], in_2[3], in_1[3]);
  and and_6 (out_3[2], in_2[2], in_1[2]);
  and and_7 (out_3[1], in_2[1], in_1[1]);
  and and_8 (out_3[0], in_2[0], in_1[0]);
endmodule

module OR_8b (
  input  [7:0] in_1,
  input  [7:0] in_2,
  output [7:0] out_3
);

  or or_1 (out_3[7], in_2[7], in_1[7]);
  or or_2 (out_3[6], in_2[6], in_1[6]);
  or or_3 (out_3[5], in_2[5], in_1[5]);
  or or_4 (out_3[4], in_2[4], in_1[4]);
  or or_5 (out_3[3], in_2[3], in_1[3]);
  or or_6 (out_3[2], in_2[2], in_1[2]);
  or or_7 (out_3[1], in_2[1], in_1[1]);
  or or_8 (out_3[0], in_2[0], in_1[0]);
endmodule

module right_shift_8b (
  input  [7:0] in_1,
  input  Arithmetic,
  input  [2:0] shamt,
  output [7:0] out_4
);

  wire multiplexer_1_out, multiplexer_2_out, multiplexer_3_out, multiplexer_4_out, multiplexer_5_out,
       multiplexer_6_out, multiplexer_7_out, multiplexer_8_out, multiplexer_9_out, multiplexer_10_out,
       multiplexer_11_out, multiplexer_12_out, multiplexer_13_out, multiplexer_14_out, multiplexer_15_out,
       multiplexer_16_out, multiplexer_17_out;

  Multiplexer #(.enable("false")) multiplexer_1 (.in0(1'b0), .in1(in_1[7]), .out(multiplexer_1_out), .sel(Arithmetic));
  Multiplexer #(.enable("false")) multiplexer_2 (.in0(in_1[0]), .in1(in_1[1]), .out(multiplexer_2_out), .sel(shamt[0]));
  Multiplexer #(.enable("false")) multiplexer_3 (.in0(in_1[1]), .in1(in_1[2]), .out(multiplexer_3_out), .sel(shamt[0]));
  Multiplexer #(.enable("false")) multiplexer_4 (.in0(in_1[2]), .in1(in_1[3]), .out(multiplexer_4_out), .sel(shamt[0]));
  Multiplexer #(.enable("false")) multiplexer_5 (.in0(in_1[3]), .in1(in_1[4]), .out(multiplexer_5_out), .sel(shamt[0]));
  Multiplexer #(.enable("false")) multiplexer_6 (.in0(in_1[4]), .in1(in_1[5]), .out(multiplexer_6_out), .sel(shamt[0]));
  Multiplexer #(.enable("false")) multiplexer_7 (.in0(in_1[5]), .in1(in_1[6]), .out(multiplexer_7_out), .sel(shamt[0]));
  Multiplexer #(.enable("false")) multiplexer_8 (.in0(in_1[6]), .in1(in_1[7]), .out(multiplexer_8_out), .sel(shamt[0]));
  Multiplexer #(.enable("false")) multiplexer_9 (
    .in0(in_1[7]), .in1(multiplexer_1_out), .out(multiplexer_9_out), .sel(shamt[0]));
  Multiplexer #(.enable("false")) multiplexer_10 (
    .in0(multiplexer_2_out), .in1(multiplexer_4_out), .out(multiplexer_10_out), .sel(shamt[1]));
  Multiplexer #(.enable("false")) multiplexer_11 (
    .in0(multiplexer_3_out), .in1(multiplexer_5_out), .out(multiplexer_11_out), .sel(shamt[1]));
  Multiplexer #(.enable("false")) multiplexer_12 (
    .in0(multiplexer_4_out), .in1(multiplexer_6_out), .out(multiplexer_12_out), .sel(shamt[1]));
  Multiplexer #(.enable("false")) multiplexer_13 (
    .in0(multiplexer_5_out), .in1(multiplexer_7_out), .out(multiplexer_13_out), .sel(shamt[1]));
  Multiplexer #(.enable("false")) multiplexer_14 (
    .in0(multiplexer_6_out), .in1(multiplexer_8_out), .out(multiplexer_14_out), .sel(shamt[1]));
  Multiplexer #(.enable("false")) multiplexer_15 (
    .in0(multiplexer_7_out), .in1(multiplexer_9_out), .out(multiplexer_15_out), .sel(shamt[1]));
  Multiplexer #(.enable("false")) multiplexer_16 (
    .in0(multiplexer_8_out), .in1(multiplexer_1_out), .out(multiplexer_16_out), .sel(shamt[1]));
  Multiplexer #(.enable("false")) multiplexer_17 (
    .in0(multiplexer_9_out), .in1(multiplexer_1_out), .out(multiplexer_17_out), .sel(shamt[1]));
  Multiplexer #(.enable("false")) multiplexer_18 (
    .in0(multiplexer_10_out), .in1(multiplexer_14_out), .out(out_4[0]), .sel(shamt[2]));
  Multiplexer #(.enable("false")) multiplexer_19 (
    .in0(multiplexer_11_out), .in1(multiplexer_15_out), .out(out_4[1]), .sel(shamt[2]));
  Multiplexer #(.enable("false")) multiplexer_20 (
    .in0(multiplexer_12_out), .in1(multiplexer_16_out), .out(out_4[2]), .sel(shamt[2]));
  Multiplexer #(.enable("false")) multiplexer_21 (
    .in0(multiplexer_13_out), .in1(multiplexer_17_out), .out(out_4[3]), .sel(shamt[2]));
  Multiplexer #(.enable("false")) multiplexer_22 (
    .in0(multiplexer_14_out), .in1(multiplexer_1_out), .out(out_4[4]), .sel(shamt[2]));
  Multiplexer #(.enable("false")) multiplexer_23 (
    .in0(multiplexer_15_out), .in1(multiplexer_1_out), .out(out_4[5]), .sel(shamt[2]));
  Multiplexer #(.enable("false")) multiplexer_24 (
    .in0(multiplexer_16_out), .in1(multiplexer_1_out), .out(out_4[6]), .sel(shamt[2]));
  Multiplexer #(.enable("false")) multiplexer_25 (
    .in0(multiplexer_17_out), .in1(multiplexer_1_out), .out(out_4[7]), .sel(shamt[2]));
endmodule

module left_shift_8b (
  input  [7:0] in_1,
  input  Arithmetic,
  input  [2:0] shamt,
  output [7:0] out_4
);

  wire multiplexer_1_out, multiplexer_2_out, multiplexer_3_out, multiplexer_4_out, multiplexer_5_out,
       multiplexer_6_out, multiplexer_7_out, multiplexer_8_out, multiplexer_9_out, multiplexer_10_out,
       multiplexer_11_out, multiplexer_12_out, multiplexer_13_out, multiplexer_14_out, multiplexer_15_out,
       multiplexer_16_out, multiplexer_17_out;

  Multiplexer #(.enable("false")) multiplexer_1 (.in0(1'b0), .in1(in_1[0]), .out(multiplexer_1_out), .sel(Arithmetic));
  Multiplexer #(.enable("false")) multiplexer_2 (.in0(in_1[7]), .in1(in_1[6]), .out(multiplexer_2_out), .sel(shamt[0]));
  Multiplexer #(.enable("false")) multiplexer_3 (.in0(in_1[6]), .in1(in_1[5]), .out(multiplexer_3_out), .sel(shamt[0]));
  Multiplexer #(.enable("false")) multiplexer_4 (.in0(in_1[5]), .in1(in_1[4]), .out(multiplexer_4_out), .sel(shamt[0]));
  Multiplexer #(.enable("false")) multiplexer_5 (.in0(in_1[4]), .in1(in_1[3]), .out(multiplexer_5_out), .sel(shamt[0]));
  Multiplexer #(.enable("false")) multiplexer_6 (.in0(in_1[3]), .in1(in_1[2]), .out(multiplexer_6_out), .sel(shamt[0]));
  Multiplexer #(.enable("false")) multiplexer_7 (.in0(in_1[2]), .in1(in_1[1]), .out(multiplexer_7_out), .sel(shamt[0]));
  Multiplexer #(.enable("false")) multiplexer_8 (.in0(in_1[1]), .in1(in_1[0]), .out(multiplexer_8_out), .sel(shamt[0]));
  Multiplexer #(.enable("false")) multiplexer_9 (
    .in0(in_1[0]), .in1(multiplexer_1_out), .out(multiplexer_9_out), .sel(shamt[0]));
  Multiplexer #(.enable("false")) multiplexer_10 (
    .in0(multiplexer_2_out), .in1(multiplexer_4_out), .out(multiplexer_10_out), .sel(shamt[1]));
  Multiplexer #(.enable("false")) multiplexer_11 (
    .in0(multiplexer_3_out), .in1(multiplexer_5_out), .out(multiplexer_11_out), .sel(shamt[1]));
  Multiplexer #(.enable("false")) multiplexer_12 (
    .in0(multiplexer_4_out), .in1(multiplexer_6_out), .out(multiplexer_12_out), .sel(shamt[1]));
  Multiplexer #(.enable("false")) multiplexer_13 (
    .in0(multiplexer_5_out), .in1(multiplexer_7_out), .out(multiplexer_13_out), .sel(shamt[1]));
  Multiplexer #(.enable("false")) multiplexer_14 (
    .in0(multiplexer_6_out), .in1(multiplexer_8_out), .out(multiplexer_14_out), .sel(shamt[1]));
  Multiplexer #(.enable("false")) multiplexer_15 (
    .in0(multiplexer_7_out), .in1(multiplexer_9_out), .out(multiplexer_15_out), .sel(shamt[1]));
  Multiplexer #(.enable("false")) multiplexer_16 (
    .in0(multiplexer_8_out), .in1(multiplexer_1_out), .out(multiplexer_16_out), .sel(shamt[1]));
  Multiplexer #(.enable("false")) multiplexer_17 (
    .in0(multiplexer_9_out), .in1(multiplexer_1_out), .out(multiplexer_17_out), .sel(shamt[1]));
  Multiplexer #(.enable("false")) multiplexer_18 (
    .in0(multiplexer_10_out), .in1(multiplexer_14_out), .out(out_4[7]), .sel(shamt[2]));
  Multiplexer #(.enable("false")) multiplexer_19 (
    .in0(multiplexer_11_out), .in1(multiplexer_15_out), .out(out_4[6]), .sel(shamt[2]));
  Multiplexer #(.enable("false")) multiplexer_20 (
    .in0(multiplexer_12_out), .in1(multiplexer_16_out), .out(out_4[5]), .sel(shamt[2]));
  Multiplexer #(.enable("false")) multiplexer_21 (
    .in0(multiplexer_13_out), .in1(multiplexer_17_out), .out(out_4[4]), .sel(shamt[2]));
  Multiplexer #(.enable("false")) multiplexer_22 (
    .in0(multiplexer_14_out), .in1(multiplexer_1_out), .out(out_4[3]), .sel(shamt[2]));
  Multiplexer #(.enable("false")) multiplexer_23 (
    .in0(multiplexer_15_out), .in1(multiplexer_1_out), .out(out_4[2]), .sel(shamt[2]));
  Multiplexer #(.enable("false")) multiplexer_24 (
    .in0(multiplexer_16_out), .in1(multiplexer_1_out), .out(out_4[1]), .sel(shamt[2]));
  Multiplexer #(.enable("false")) multiplexer_25 (
    .in0(multiplexer_17_out), .in1(multiplexer_1_out), .out(out_4[0]), .sel(shamt[2]));
endmodule

module COND (
  input  z,
  input  c,
  input  n,
  input  v,
  input  s,
  input  [2:0] cond,
  output T
);

  wire and_1_out, multiplexer_1_out, not_1_out, not_2_out, not_3_out, not_4_out, not_5_out, xor_1_out;

  not not_1 (not_1_out, c);
  xor xor_1 (xor_1_out, n, v);
  Multiplexer #(.enable("false")) multiplexer_1 (.in0(not_1_out), .in1(xor_1_out), .out(multiplexer_1_out), .sel(s));
  not not_2 (not_2_out, z);
  not not_3 (not_3_out, multiplexer_1_out);
  not not_4 (not_4_out, and_1_out);
  and and_1 (and_1_out, not_2_out, not_3_out);
  not not_5 (not_5_out, n);
  Multiplexer #(.select(3), .enable("false")) multiplexer_2 (
    .in0(z), .in1(not_2_out), .in2(multiplexer_1_out), .in3(not_3_out), .in4(and_1_out), .in5(not_4_out),
    .in6(n), .in7(not_5_out), .out(T), .sel(cond));
endmodule

module ALU (
  input  [7:0] A,
  input  [7:0] B,
  input  [2:0] shamt,
  input  [2:0] opcode,
  input  unsign_sign,
  input  [2:0] COND__0____1____2___3____4___5____6_ve__7_ve,
  output T,
  output [7:0] result
);

  wire adder_8b_1_carry, adder_8b_1_overflow, and_1_out, and_2_out, nor_1_out, not_1_out, not_2_out;
  wire [7:0] adder_8b_1_out_8, and_8b_1_out_3, left_shift_8b_1_out_4, or_8b_1_out_3, right_shift_8b_1_out_4,
       xor_8b_1_out_3;

  not not_1 (not_1_out, opcode[1]);
  not not_2 (not_2_out, opcode[2]);
  and and_1 (and_1_out, opcode[0], not_1_out, not_2_out);
  and and_2 (and_2_out, opcode[0], opcode[1], opcode[2]);
  adder_8b adder_8b_1 (
    .A(A), .B(B), .Sub(and_1_out), .Carry(adder_8b_1_carry), .Overflow(adder_8b_1_overflow),
    .out_8(adder_8b_1_out_8));  // open: Zero, minus_VE
  AND_8b and_8b_1 (.in_1(A), .in_2(B), .out_3(and_8b_1_out_3));
  XOR_8b xor_8b_1 (.in_1(A), .in_2(B), .out_3(xor_8b_1_out_3));
  OR_8b or_8b_1 (.in_1(A), .in_2(B), .out_3(or_8b_1_out_3));
  left_shift_8b left_shift_8b_1 (.in_1(A), .Arithmetic(and_2_out), .shamt(shamt), .out_4(left_shift_8b_1_out_4));
  right_shift_8b right_shift_8b_1 (.in_1(A), .Arithmetic(and_2_out), .shamt(shamt), .out_4(right_shift_8b_1_out_4));
  Multiplexer #(.select(3), .width(8), .enable("false")) multiplexer_1 (
    .in0(adder_8b_1_out_8), .in1(adder_8b_1_out_8), .in2(and_8b_1_out_3), .in3(xor_8b_1_out_3),
    .in4(or_8b_1_out_3), .in5(left_shift_8b_1_out_4), .in6(right_shift_8b_1_out_4),
    .in7(right_shift_8b_1_out_4), .out(result), .sel(opcode));
  nor nor_1 (nor_1_out, result[0], result[1], result[2], result[3], result[4], result[5], result[6], result[7]);
  COND cond_1 (
    .z(nor_1_out), .c(adder_8b_1_carry), .n(result[7]), .v(adder_8b_1_overflow), .s(unsign_sign),
    .cond(COND__0____1____2___3____4___5____6_ve__7_ve), .T(T));
endmodule

module Register_8b (
  input  [7:0] in_1,
  input  Clock,
  input  Wri,
  input  clear,
  output [7:0] out_5
);

  D_Flip_Flop d_ff_1 (.clk(Clock), .D(in_1[0]), .Q(out_5[0]), .en(Wri), .reset(clear));  // open: Qn, preset
  D_Flip_Flop d_ff_2 (.clk(Clock), .D(in_1[1]), .Q(out_5[1]), .en(Wri), .reset(clear));  // open: Qn, preset
  D_Flip_Flop d_ff_3 (.clk(Clock), .D(in_1[2]), .Q(out_5[2]), .en(Wri), .reset(clear));  // open: Qn, preset
  D_Flip_Flop d_ff_4 (.clk(Clock), .D(in_1[3]), .Q(out_5[3]), .en(Wri), .reset(clear));  // open: Qn, preset
  D_Flip_Flop d_ff_5 (.clk(Clock), .D(in_1[4]), .Q(out_5[4]), .en(Wri), .reset(clear));  // open: Qn, preset
  D_Flip_Flop d_ff_6 (.clk(Clock), .D(in_1[5]), .Q(out_5[5]), .en(Wri), .reset(clear));  // open: Qn, preset
  D_Flip_Flop d_ff_7 (.clk(Clock), .D(in_1[6]), .Q(out_5[6]), .en(Wri), .reset(clear));  // open: Qn, preset
  D_Flip_Flop d_ff_8 (.clk(Clock), .D(in_1[7]), .Q(out_5[7]), .en(Wri), .reset(clear));  // open: Qn, preset
endmodule

module register_file (
  input  [7:0] Din,
  input  [2:0] WriAddr,
  input  [2:0] readAddrA,
  input  [2:0] readAddrB,
  input  WriEn,
  input  Clock,
  input  ClearAll,
  output [7:0] DoutA,
  output [7:0] DoutB
);

  wire and_1_out, and_2_out, and_3_out, and_4_out, and_5_out, and_6_out, and_7_out, decoder_1_out1,
       decoder_1_out2, decoder_1_out3, decoder_1_out4, decoder_1_out5, decoder_1_out6, decoder_1_out7;
  wire [7:0] register_8b_1_out_5, register_8b_2_out_5, register_8b_3_out_5, register_8b_4_out_5,
       register_8b_5_out_5, register_8b_6_out_5, register_8b_7_out_5;

  Decoder #(.select(3), .enable("false")) decoder_1 (
    .out1(decoder_1_out1), .out2(decoder_1_out2), .out3(decoder_1_out3), .out4(decoder_1_out4),
    .out5(decoder_1_out5), .out6(decoder_1_out6), .out7(decoder_1_out7), .sel(WriAddr));  // open: out0
  and and_1 (and_1_out, decoder_1_out1, WriEn);
  and and_2 (and_2_out, decoder_1_out2, WriEn);
  and and_3 (and_3_out, decoder_1_out3, WriEn);
  and and_4 (and_4_out, decoder_1_out4, WriEn);
  and and_5 (and_5_out, decoder_1_out5, WriEn);
  and and_6 (and_6_out, decoder_1_out6, WriEn);
  and and_7 (and_7_out, decoder_1_out7, WriEn);
  Register_8b register_8b_1 (.in_1(Din), .Clock(Clock), .Wri(and_1_out), .clear(ClearAll), .out_5(register_8b_1_out_5));
  Register_8b register_8b_2 (.in_1(Din), .Clock(Clock), .Wri(and_2_out), .clear(ClearAll), .out_5(register_8b_2_out_5));
  Register_8b register_8b_3 (.in_1(Din), .Clock(Clock), .Wri(and_3_out), .clear(ClearAll), .out_5(register_8b_3_out_5));
  Register_8b register_8b_4 (.in_1(Din), .Clock(Clock), .Wri(and_4_out), .clear(ClearAll), .out_5(register_8b_4_out_5));
  Register_8b register_8b_5 (.in_1(Din), .Clock(Clock), .Wri(and_5_out), .clear(ClearAll), .out_5(register_8b_5_out_5));
  Register_8b register_8b_6 (.in_1(Din), .Clock(Clock), .Wri(and_6_out), .clear(ClearAll), .out_5(register_8b_6_out_5));
  Register_8b register_8b_7 (.in_1(Din), .Clock(Clock), .Wri(and_7_out), .clear(ClearAll), .out_5(register_8b_7_out_5));
  Multiplexer #(.select(3), .width(8), .enable("false")) multiplexer_1 (
    .in0({8{1'b0}}), .in1(register_8b_1_out_5), .in2(register_8b_2_out_5), .in3(register_8b_3_out_5),
    .in4(register_8b_4_out_5), .in5(register_8b_5_out_5), .in6(register_8b_6_out_5),
    .in7(register_8b_7_out_5), .out(DoutA), .sel(readAddrA));
  Multiplexer #(.select(3), .width(8), .enable("false")) multiplexer_2 (
    .in0({8{1'b0}}), .in1(register_8b_1_out_5), .in2(register_8b_2_out_5), .in3(register_8b_3_out_5),
    .in4(register_8b_4_out_5), .in5(register_8b_5_out_5), .in6(register_8b_6_out_5),
    .in7(register_8b_7_out_5), .out(DoutB), .sel(readAddrB));
endmodule

module PC (
  input  [7:0] offest,
  input  [7:0] Imm,
  input  Jump,
  input  Branch,
  input  Clk,
  input  PC_load,
  input  clear,
  input  RET,
  input  JSR,
  output [7:0] PC
);

  wire or_1_out;
  wire [1:0] or_2_out;
  wire [7:0] adder_8b_1_out_8, adder_8b_2_out_8, multiplexer_1_out, register_8b_1_out_5;

  or or_1 (or_1_out, Jump, RET);
  or or_2 (or_2_out[0], Branch, RET);
  adder_8b adder_8b_1 (
    .A(PC), .B(8'h1), .Sub(1'b0), .out_8(adder_8b_1_out_8));  // open: Zero, minus_VE, Carry, Overflow
  adder_8b adder_8b_2 (
    .A(PC), .B(offest), .Sub(1'b0), .out_8(adder_8b_2_out_8));  // open: Zero, minus_VE, Carry, Overflow
  or or_3 (or_2_out[1], JSR, or_1_out);
  Register_8b register_8b_1 (
    .in_1(adder_8b_1_out_8), .Clock(Clk), .Wri(JSR), .clear(clear), .out_5(register_8b_1_out_5));
  Multiplexer #(.select(2), .width(8), .enable("false")) multiplexer_1 (
    .in0(adder_8b_1_out_8), .in1(adder_8b_2_out_8), .in2(Imm), .in3(register_8b_1_out_5),
    .out(multiplexer_1_out), .sel(or_2_out));
  Register_8b register_8b_2 (.in_1(multiplexer_1_out), .Clock(Clk), .Wri(PC_load), .clear(clear), .out_5(PC));
endmodule

module control_unit (
  input  [31:0] in_1,
  input  T,
  output Jump,
  output Branch,
  output RET,
  output JSR,
  output PC_load,
  output [2:0] WriAddr,
  output [2:0] ReadAddrA,
  output [2:0] ReadAddrB,
  output WriEn,
  output [2:0] ALU_shamt,
  output [2:0] ALU_opcode,
  output UnSigned__Signed,
  output [2:0] COND,
  output [7:0] Imm,
  output is_imm,
  output RAM_Wri,
  output RAM_load,
  output RAM_to_Reg
);

  wire and_2_out, and_3_out, decoder_1_out0, decoder_1_out2, not_1_out, not_2_out, not_3_out, not_4_out,
       not_5_out, not_6_out, not_7_out, not_8_out;

  Decoder #(.select(3), .enable("false")) decoder_1 (
    .out0(decoder_1_out0), .out1(Jump), .out2(decoder_1_out2), .out3(RET), .out4(JSR), .sel(in_1[5:3]));  // open: out5, out6, out7
  not not_1 (not_1_out, in_1[1]);
  not not_2 (not_2_out, in_1[2]);
  not not_3 (not_3_out, in_1[0]);
  and and_1 (UnSigned__Signed, not_3_out, in_1[1], in_1[2]);
  and and_2 (and_2_out, in_1[2], not_1_out);
  or or_1 (is_imm, and_2_out, and_3_out);
  and and_3 (and_3_out, in_1[0], not_2_out);
  and and_4 (RAM_load, in_1[2], not_4_out, not_5_out);
  not not_4 (not_4_out, in_1[0]);
  not not_5 (not_5_out, in_1[1]);
  and and_5 (RAM_Wri, in_1[0], not_6_out, in_1[2]);
  not not_6 (not_6_out, in_1[1]);
  and and_6 (Branch, decoder_1_out2, T);
  or or_2 (PC_load, JSR, RET, decoder_1_out2, Jump, decoder_1_out0);
  not not_7 (not_7_out, in_1[0]);
  not not_8 (not_8_out, in_1[2]);
  or or_3 (WriEn, not_7_out, not_8_out);

  assign ALU_opcode = in_1[19:17];
  assign ALU_shamt = in_1[22:20];
  assign COND = in_1[16:14];
  assign Imm = in_1[13:6];
  assign RAM_to_Reg = RAM_load;
  assign ReadAddrA = in_1[28:26];
  assign ReadAddrB = in_1[25:23];
  assign WriAddr = in_1[31:29];
endmodule
